# Fritzing sketch LED to Bag (saved by Fritzing 0.9.3b)
breadboards: 1

parts:
  Arduino_UNO = Arduino Uno (Rev3)
  L3 = LED - 5mm [color="Green (555nm)" package="5 mm [THT]"]
  R1 = Resistor [tolerance=±5% resistance=220 package=THT]
  L2 = LED - 5mm [color="Green (555nm)" package="5 mm [THT]"]
  R2 = Resistor [tolerance=±5% resistance=220 package=THT]
  L1 = LED - 5mm [color="Green (555nm)" package="5 mm [THT]"]
  R3 = Resistor [tolerance=±5% resistance=220 package=THT]
  R4 = Resistor [tolerance=±5% resistance=100 package=THT]
  R5 = Resistor [tolerance=±5% resistance=220 package=THT]
  L_R = LED - 5mm [color="Red (633nm)" package="5 mm [THT]"]
  L_B = LED - 5mm [color="White (4500K)" package="5 mm [THT]"]
  T_D = Pushbutton [package="[THT]"]
  Pot = Rotary Potentiometer (Small) [maximum_resistance=100kΩ package=THT]
  T_S = Pushbutton [package="[THT]"]
  R6 = Resistor [tolerance=±5% resistance=10k package=THT]
  R_S = Resistor [tolerance=±5% resistance=10k package=THT]

nets:
  N1: Arduino_UNO.A0, Pot.wiper
  N2: Arduino_UNO.D8, R3.Pin_0
  N3: Arduino_UNO.D12/MISO, R2.Pin_0
  N4: Arduino_UNO.D13/SCK, R1.Pin_0
  N5: Arduino_UNO.D2, T_D.Pin_3, T_D.Pin_4, R_S.Pin_1
  N6: Arduino_UNO.D3_PWM, T_S.Pin_3, T_S.Pin_4, R6.Pin_1
  N7: Arduino_UNO.D4, R5.Pin_0
  N8: Arduino_UNO.D6_PWM, R4.Pin_0
  N9: Arduino_UNO.5V, T_D.Pin_1, T_D.Pin_2, Pot.leg2, T_S.Pin_1, T_S.Pin_2
  N10: Arduino_UNO.GND, L3.cathode, L2.cathode, L1.cathode, L_R.cathode, L_B.cathode, Pot.leg1, R6.Pin_0, R_S.Pin_0
  N11: L3.anode, R1.Pin_1
  N12: L2.anode, R2.Pin_1
  N13: L1.anode, R3.Pin_1
  N14: R4.Pin_1, L_B.anode
  N15: R5.Pin_1, L_R.anode

// code stored in the sketch: Untitled2.ino

