# Fritzing sketch smart_radar (saved by Fritzing 0.9.2b)
breadboards: 1

parts:
  R2 = Rotary Potentiometer (Small) [maximum_resistance=100kΩ package=THT]
  Componente2 = SRF05 Ultrasonic Rangefinder
  S3 = Pushbutton [package="[THT]"]
  R11 = Resistor [tolerance=±5% resistance=220 package="2512 [SMD]"]
  S2 = Pushbutton [package="[THT]"]
  PIR1 = PIR sensor
  R9 = Resistor [tolerance=±5% resistance=10k package=THT]
  L_a = smd LED [color="Red (633nm)" package="0603 [SMD]"]
  R7 = Resistor [tolerance=±5% resistance=10k package=THT]
  R10 = Resistor [tolerance=±5% resistance=220 package="2512 [SMD]"]
  L_d = smd LED [color="Red (633nm)" package="0603 [SMD]"]
  S1 = Pushbutton [package="[THT]"]
  Componente1 = Arduino Uno (Rev3)
  J1 = Basic Servo
  R8 = Resistor [tolerance=±5% resistance=10k package=THT]

nets:
  GND: R2.leg1, Componente2.GND, PIR1.GND, R9.Pin_0, L_a.cathode, R7.Pin_0, L_d.cathode, Componente1.GND, J1.gnd, R8.Pin_0
  N1: R2.wiper, Componente1.A5/SCL
  VCC: R2.leg2, Componente2.VCC, S3.Pin_1, S3.Pin_2, S2.Pin_1, S2.Pin_2, PIR1.VDD, S1.Pin_1, S1.Pin_2, Componente1.5V, J1.vcc
  N2: Componente2.Trig, Componente1.D3_PWM
  N3: Componente2.Echo, Componente1.D4
  N4: S3.Pin_3, S3.Pin_4, Componente1.D6_PWM, R8.Pin_1
  N5: R11.Pin_0, L_d.anode
  N6: R11.Pin_1, Componente1.D9_PWM
  N7: S2.Pin_3, S2.Pin_4, R9.Pin_1, Componente1.D7
  N8: PIR1.SIG, Componente1.D2
  N9: L_a.anode, R10.Pin_0
  N10: R7.Pin_1, S1.Pin_3, S1.Pin_4, Componente1.D5_PWM
  N11: R10.Pin_1, Componente1.D8
  N12: Componente1.D13/SCK, J1.pulse
